// Logisim project Matheus Endlich Silveira- MCU_4bits_CC3MB_24.circ as structural Verilog: 5 circuits, main circuit main
module main (
  input  [3:0] A,
  input  [3:0] B,
  output Overflow,
  output Overflow_2,
  output [3:0] Saida,
  output [3:0] Saida_2
);

  Add_4 add_4_1 (.in_2(A), .Vem_1(Overflow), .in_1(B), .Vem__1(1'b0), .out_5(Saida));
  Sub_4 sub_4_1 (.A(A), .Overflow(Overflow_2), .B(B), .Vem_1(1'b0), .out_5(Saida_2));
endmodule

module Add_1 (
  input  A,
  input  B,
  input  Vem_1,
  output Saida,
  output Vai_1
);

  wire and_1_out, and_2_out, or_1_out, xor_1_out;

  xor xor_1 (xor_1_out, A, B);
  or or_1 (or_1_out, B, Vem_1);
  xor xor_2 (Saida, xor_1_out, Vem_1);
  and and_1 (and_1_out, or_1_out, A);
  and and_2 (and_2_out, B, Vem_1);
  or or_2 (Vai_1, and_1_out, and_2_out);
endmodule

module Add_4 (
  input  [3:0] in_1,
  input  [3:0] in_2,
  input  Vem__1,
  output Vem_1,
  output [3:0] out_5
);

  wire add_1_2_vai_1, add_1_3_vai_1, add_1_4_vai_1;

  Add_1 add_1_1 (.A(in_2[3]), .B(in_1[3]), .Vem_1(add_1_2_vai_1), .Saida(out_5[3]), .Vai_1(Vem_1));
  Add_1 add_1_2 (.A(in_2[2]), .B(in_1[2]), .Vem_1(add_1_3_vai_1), .Saida(out_5[2]), .Vai_1(add_1_2_vai_1));
  Add_1 add_1_3 (.A(in_2[1]), .B(in_1[1]), .Vem_1(add_1_4_vai_1), .Saida(out_5[1]), .Vai_1(add_1_3_vai_1));
  Add_1 add_1_4 (.A(in_2[0]), .B(in_1[0]), .Vem_1(Vem__1), .Saida(out_5[0]), .Vai_1(add_1_4_vai_1));
endmodule

module Sub_1 (
  input  A,
  input  B,
  input  Vem_1,
  output Saida,
  output Vai_1
);

  wire and_1_out, and_2_out, not_1_out, or_1_out, xor_1_out;

  not not_1 (not_1_out, A);
  xor xor_1 (xor_1_out, A, B);
  or or_1 (or_1_out, B, Vem_1);
  xor xor_2 (Saida, xor_1_out, Vem_1);
  and and_1 (and_1_out, or_1_out, not_1_out);
  and and_2 (and_2_out, B, Vem_1);
  or or_2 (Vai_1, and_1_out, and_2_out);
endmodule

module Sub_4 (
  input  [3:0] B,
  input  [3:0] A,
  input  Vem_1,
  output Overflow,
  output [3:0] out_5
);

  wire sub_1_2_vai_1, sub_1_3_vai_1, sub_1_4_vai_1;

  Sub_1 sub_1_1 (.A(A[3]), .B(B[3]), .Vem_1(sub_1_2_vai_1), .Saida(out_5[3]), .Vai_1(Overflow));
  Sub_1 sub_1_2 (.A(A[2]), .B(B[2]), .Vem_1(sub_1_3_vai_1), .Saida(out_5[2]), .Vai_1(sub_1_2_vai_1));
  Sub_1 sub_1_3 (.A(A[1]), .B(B[1]), .Vem_1(sub_1_4_vai_1), .Saida(out_5[1]), .Vai_1(sub_1_3_vai_1));
  Sub_1 sub_1_4 (.A(A[0]), .B(B[0]), .Vem_1(Vem_1), .Saida(out_5[0]), .Vai_1(sub_1_4_vai_1));
endmodule
